# Fritzing sketch adsr (saved by Fritzing 0.8.7b)
circuit board: 5.00019cm x 5cm
circuit board: 5.00019cm x 5cm
breadboards: 1

parts:
  J506 = female pin header, 6 pins [form="♀ (female)"]
  J507 = female pin header, 6 pins [form="♀ (female)"]
  J508 = female pin header, 4 pins [form="♀ (female)"]
  J509 = female pin header, 4 pins [form="♀ (female)"]
  J510 = female pin header, 4 pins [form="♀ (female)"]
  J511 = female pin header, 4 pins [form="♀ (female)"]
  J512 = female pin header, 4 pins [form="♀ (female)"]
  J513 = female pin header, 4 pins [form="♀ (female)"]
  J514 = female pin header, 4 pins [form="♀ (female)"]
  J515 = female pin header, 4 pins [form="♀ (female)"]
  J516 = female pin header, 6 pins [form="♀ (female)"]
  J517 = female pin header, 6 pins [form="♀ (female)"]
  J518 = female pin header, 2 pins [form="♀ (female)"]
  J519 = female pin header, 2 pins [form="♀ (female)"]
  J520 = double row female pin header, 4 pins [form="♀ (female)"]
  Part20 = Arduino Nano (Rev3.0)
  R114 = Resistor [tolerance=±5% resistance=10k package=THT]
  R115 = Resistor [tolerance=±5% resistance=10k package=THT]
  R116 = Resistor [tolerance=±5% resistance=10k package=THT]
  R117 = Resistor [tolerance=±5% resistance=10k package=THT]

nets:
  N1: J506.pin1, J510.pin4
  N2: J506.pin2, J513.pin1
  N3: J506.pin3, J513.pin3, J514.pin3
  N4: J506.pin4, J511.pin4
  N5: J506.pin5, J510.pin1, J510.pin3, J511.pin1, J511.pin3
  N6: J506.pin6, J508.pin1
  N7: J507.pin1, J514.pin1
  N8: J507.pin2, J512.pin1
  N9: J507.pin3, J508.pin3, J512.pin3
  N10: J507.pin4, J515.pin4
  N11: J507.pin5, J509.pin1, J509.pin3, J515.pin1, J515.pin3
  N12: J507.pin6, J509.pin4
  N13: J516.pin1, R116.Pin_1
  N14: J516.pin2, R117.Pin_0
  N15: J516.pin3, J517.pin3, J520.pin2, Part20.5V
  N16: J516.pin4, Part20.A1
  N17: J516.pin5, J517.pin5, J518.pin2, J520.pin1, Part20.GND
  N18: J516.pin6, Part20.A3
  N19: J517.pin1, Part20.A2
  N20: J517.pin2, R115.Pin_0
  N21: J517.pin4, Part20.A0
  N22: J517.pin6, R114.Pin_1
  N23: J518.pin1, Part20.3V3
  N24: J519.pin1, Part20.D1/TX
  N25: J519.pin2, Part20.D0/RX
  N26: J520.pin3, Part20.D2
  N27: J520.pin4, Part20.D3
  N28: Part20.D5, R114.Pin_0
  N29: Part20.D6, R117.Pin_1
  N30: Part20.D9, R115.Pin_1
  N31: Part20.D10, R116.Pin_0

notes:
  L
  2
  SLD3 -> A0
  LED2 <- D5
  SLD2 -> A3
  SLD1 -> A1
  LED1 <- 6
  LED3 <- 9
  ->ARD GND
  -> ARD GND
  1
  ->ARD 5V
  3
  SLD4 -> A2
  LED4 <-10
  B
  -> ARD 5V
  E
  Dreamer Nano v4.0
  ARD 5V
  v2.0
  SLD2->A3
  LED2<-D5
  D13
  ARD GND
  SLD1->A1
  LED3->D9
  SLD3->A0
  LED1<-D6
  LED4<-D10
  SLD4->A2
  Rx
  Tx
  3.3V
  GND
  --I2C--
  220
  +
  this board is attached upside down to the other board
