# Fritzing sketch binome (saved by Fritzing 0.8.7b)
circuit board: 5.00019cm x 5cm
circuit board: 5.00019cm x 5cm
breadboards: 1

parts:
  Part14 = Arduino Nano (Rev3.0)
  J451 = female pin header, 4 pins [form="♀ (female)"]
  J452 = female pin header, 4 pins [form="♀ (female)"]
  J453 = female pin header, 4 pins [form="♀ (female)"]
  J454 = double row female pin header, 4 pins [form="♀ (female)"]
  R102 = Resistor [tolerance=±5% resistance=10k package=THT]
  R103 = Resistor [tolerance=±5% resistance=10k package=THT]
  R104 = Resistor [tolerance=±5% resistance=10k package=THT]
  R105 = Resistor [tolerance=±5% resistance=10k package=THT]
  R106 = Resistor [tolerance=±5% resistance=10k package=THT]
  R107 = Resistor [tolerance=±5% resistance=10k package=THT]
  R108 = Resistor [tolerance=±5% resistance=10k package=THT]
  R109 = Resistor [tolerance=±5% resistance=10k package=THT]
  J455 = female pin header, 2 pins [form="♀ (female)"]
  J456 = female pin header, 2 pins [form="♀ (female)"]
  U1 = BUTTONPAD-2X2 [package=buttonpad-2x2-special]  # not connected

nets:
  N1: Part14.D1/TX, J456.pin1
  N2: Part14.D0/RX, J456.pin2
  N3: Part14.GND, J454.pin1, R102.Pin_1, R103.Pin_1, R104.Pin_1, R105.Pin_1, R106.Pin_0, R107.Pin_0, R108.Pin_0, R109.Pin_0, J455.pin2
  N4: Part14.D2, J454.pin3
  N5: Part14.D3, J454.pin4
  N6: Part14.D4, J453.pin2, R107.Pin_1
  N7: Part14.D5, J453.pin3, R108.Pin_1
  N8: Part14.D6, J453.pin4, R109.Pin_1
  N9: Part14.D7, J452.pin4, R103.Pin_0
  N10: Part14.D8, J452.pin3, R105.Pin_0
  N11: Part14.D9, J451.pin1
  N12: Part14.D10, J451.pin2
  N13: Part14.D11/MOSI, J451.pin3
  N14: Part14.D12/MISO, J452.pin2, R104.Pin_0
  N15: Part14.5V, J451.pin4, J454.pin2
  N16: Part14.A3, J453.pin1, R106.Pin_1
  N17: Part14.3V3, J455.pin1
  N18: Part14.D13/SCK, J452.pin1, R102.Pin_0

notes:
  10k
  D13
  330
  LED-GND4
  SWT-GND4
  v2.0
  GND
  --I2C--
  SWT-GND1
  SWT-GND3
  LED-GND1
  LED-GND3
  LED-GND2
  SWT-GND2
  2
  +
  3
  Rx
  Tx
  3.3V
  this board is attached upside down to the other board
  this board was created by N.Seidle in Eagle and it is not available in Frizting. This is just for reference.
