# Fritzing sketch locketRauncher (saved by Fritzing 0.8.7b)
circuit board: 5.00019cm x 5cm
breadboards: 1

parts:
  Part23 = Arduino Nano (Rev3.0)
  J585 = female pin header, 2 pins [form="♀ (female)"]
  J586 = female pin header, 2 pins [form="♀ (female)"]
  J587 = female pin header, 2 pins [form="♀ (female)"]
  J588 = female pin header, 2 pins [form="♀ (female)"]
  J589 = female pin header, 1 pin [form="♀ (female)"]
  J590 = female pin header, 1 pin [form="♀ (female)"]
  J591 = female pin header, 1 pin [form="♀ (female)"]
  J592 = female pin header, 1 pin [form="♀ (female)"]
  J593 = female pin header, 1 pin [form="♀ (female)"]
  J594 = female pin header, 1 pin [form="♀ (female)"]
  J595 = female pin header, 1 pin [form="♀ (female)"]
  J596 = female pin header, 1 pin [form="♀ (female)"]
  J597 = female pin header, 1 pin [form="♀ (female)"]
  J598 = female pin header, 1 pin [form="♀ (female)"]
  J599 = female pin header, 1 pin [form="♀ (female)"]
  J600 = female pin header, 1 pin [form="♀ (female)"]
  R194 = Resistor [tolerance=±5% resistance=10k package=THT]
  R195 = Resistor [tolerance=±5% resistance=10k package=THT]
  R196 = Resistor [tolerance=±5% resistance=10k package=THT]
  R197 = Resistor [tolerance=±5% resistance=10k package=THT]
  R198 = Resistor [tolerance=±5% resistance=10k package=THT]
  R199 = Resistor [tolerance=±5% resistance=10k package=THT]
  R200 = Resistor [tolerance=±5% resistance=10k package=THT]
  R201 = Resistor [tolerance=±5% resistance=10k package=THT]
  J601 = double row female pin header, 4 pins [form="♀ (female)"]
  J602 = female pin header, 2 pins [form="♀ (female)"]
  J603 = female pin header, 2 pins [form="♀ (female)"]
  R202 = Resistor [tolerance=±5% resistance=10k package=THT]
  R203 = Resistor [tolerance=±5% resistance=10k package=THT]
  R204 = Resistor [tolerance=±5% resistance=10k package=THT]
  R205 = Resistor [tolerance=±5% resistance=10k package=THT]

nets:
  N1: Part23.D1/TX, J603.pin1
  N2: Part23.D0/RX, J603.pin2
  N3: Part23.GND, J585.pin2, J586.pin2, J587.pin2, J588.pin2, J597.pin1, J598.pin1, J599.pin1, J600.pin1, J601.pin1, J602.pin2
  N4: Part23.D2, J601.pin3
  N5: Part23.D3, R205.Pin_1
  N6: Part23.D4, J591.pin1, R195.Pin_1
  N7: Part23.D5, R203.Pin_1
  N8: Part23.D6, J588.pin1
  N9: Part23.D7, J595.pin1, R197.Pin_1
  N10: Part23.D8, J593.pin1, R200.Pin_0
  N11: Part23.D9, R202.Pin_0
  N12: Part23.D10, R204.Pin_0
  N13: Part23.D11/MOSI, J590.pin1, R194.Pin_0
  N14: Part23.D12/MISO, J594.pin1, R196.Pin_0
  N15: Part23.5V, R194.Pin_1, R195.Pin_0, R196.Pin_1, R197.Pin_0, R198.Pin_0, R199.Pin_0, R200.Pin_1, R201.Pin_1, J601.pin2
  N16: Part23.A1, J592.pin1, R199.Pin_1
  N17: Part23.A0, J596.pin1, R198.Pin_1
  N18: Part23.3V3, J602.pin1
  N19: Part23.D13/SCK, J589.pin1, R201.Pin_0
  N20: J585.pin1, R204.Pin_1
  N21: J586.pin1, R202.Pin_1
  N22: J587.pin1, R203.Pin_0
  N23: J601.pin4, R205.Pin_0

notes:
  10k
  D13
  GND
  --I2C--
  +
  2
  3
  LED1>D6
  LED3>D10
  LED4>D9
  LED2>D5
  Rx
  >D12
  >D7
  T3/A
  T2/A
  T4/B
  T4/A
  3.3V
  >D11
  T3/B
  >D13
  >D8
  >D4
  T2/B
  Tx
  >A1
  T1/A
  >A0
  T1/B
  220
