# Fritzing sketch o (saved by Fritzing 0.8.7b)
circuit board: 5.00019cm x 5cm
circuit board: 5.00019cm x 5cm
circuit board: 5cm x 5cm
breadboards: 1

parts:
  U19 = 74HC595 [package="DIP16 [THT]"]
  U20 = 74HC595 [package="DIP16 [THT]"]
  U21 = 74HC595 [package="DIP16 [THT]"]
  C15 = Ceramic Capacitor [capacitance=100nF package="100 mil [THT, multilayer]"]
  Part18 = Arduino Nano (Rev3.0)
  J465 = female pin header, 2 pins [form="♀ (female)"]
  J466 = female pin header, 2 pins [form="♀ (female)"]
  J467 = female pin header, 4 pins [form="♀ (female)"]
  J468 = female pin header, 4 pins [form="♀ (female)"]
  J469 = female pin header, 4 pins [form="♀ (female)"]
  J470 = female pin header, 4 pins [form="♀ (female)"]
  J471 = female pin header, 4 pins [form="♀ (female)"]
  J472 = female pin header, 4 pins [form="♀ (female)"]
  J473 = female pin header, 4 pins [form="♀ (female)"]
  J474 = double row female pin header, 4 pins [form="♀ (female)"]
  R91 = Resistor [tolerance=±5% resistance=220 package=THT]
  R92 = Resistor [tolerance=±5% resistance=220 package=THT]
  R93 = Resistor [tolerance=±5% resistance=220 package=THT]
  R94 = Resistor [tolerance=±5% resistance=220 package=THT]
  R95 = Resistor [tolerance=±5% resistance=220 package=THT]
  R96 = Resistor [tolerance=±5% resistance=220 package=THT]
  R97 = Resistor [tolerance=±5% resistance=220 package=THT]
  R98 = Resistor [tolerance=±5% resistance=220 package=THT]
  R99 = Resistor [tolerance=±5% resistance=220 package=THT]
  R100 = Resistor [tolerance=±5% resistance=220 package=THT]
  R101 = Resistor [tolerance=±5% resistance=220 package=THT]
  R102 = Resistor [tolerance=±5% resistance=220 package=THT]
  R103 = Resistor [tolerance=±5% resistance=220 package=THT]
  R104 = Resistor [tolerance=±5% resistance=220 package=THT]
  R105 = Resistor [tolerance=±5% resistance=220 package=THT]
  R106 = Resistor [tolerance=±5% resistance=220 package=THT]
  R107 = Resistor [tolerance=±5% resistance=220 package=THT]
  R108 = Resistor [tolerance=±5% resistance=220 package=THT]
  R109 = Resistor [tolerance=±5% resistance=220 package=THT]
  R110 = Resistor [tolerance=±5% resistance=220 package=THT]
  R111 = Resistor [tolerance=±5% resistance=220 package=THT]
  R112 = Resistor [tolerance=±5% resistance=220 package=THT]
  R113 = Resistor [tolerance=±5% resistance=220 package=THT]
  R114 = Resistor [tolerance=±5% resistance=220 package=THT]
  RE5 = Rotary Encoder [package=THT]
  J475 = female pin header, 8 pins [form="♀ (female)"]
  J476 = female pin header, 8 pins [form="♀ (female)"]
  J477 = female pin header, 4 pins [form="♀ (female)"]
  J478 = female pin header, 4 pins [form="♀ (female)"]
  J479 = female pin header, 4 pins [form="♀ (female)"]
  J480 = female pin header, 4 pins [form="♀ (female)"]
  J481 = female pin header, 4 pins [form="♀ (female)"]
  J482 = female pin header, 4 pins [form="♀ (female)"]
  J483 = female pin header, 8 pins [form="♀ (female)"]
  J484 = female pin header, 8 pins [form="♀ (female)"]
  J485 = female pin header, 8 pins [form="♀ (female)"]
  J486 = female pin header, 8 pins [form="♀ (female)"]
  J487 = female pin header, 4 pins [form="♀ (female)"]
  J488 = female pin header, 4 pins [form="♀ (female)"]
  J489 = female pin header, 1 pin [form="♀ (female)"]
  J490 = female pin header, 1 pin [form="♀ (female)"]
  LED48 = smd LED [color="Red (633nm)" package="1206 [SMD]"]
  LED49 = smd LED [color="Red (633nm)" package="1206 [SMD]"]
  LED50 = smd LED [color="Red (633nm)" package="1206 [SMD]"]
  LED51 = smd LED [color="Red (633nm)" package="1206 [SMD]"]
  LED52 = smd LED [color="Red (633nm)" package="1206 [SMD]"]
  LED53 = smd LED [color="Red (633nm)" package="1206 [SMD]"]
  LED54 = smd LED [color="Red (633nm)" package="1206 [SMD]"]
  LED55 = smd LED [color="Red (633nm)" package="1206 [SMD]"]
  LED56 = smd LED [color="Red (633nm)" package="1206 [SMD]"]
  LED57 = smd LED [color="Red (633nm)" package="1206 [SMD]"]
  LED58 = smd LED [color="Red (633nm)" package="1206 [SMD]"]
  LED59 = smd LED [color="Red (633nm)" package="1206 [SMD]"]
  LED60 = smd LED [color="Red (633nm)" package="1206 [SMD]"]
  LED61 = smd LED [color="Red (633nm)" package="1206 [SMD]"]
  LED62 = smd LED [color="Red (633nm)" package="1206 [SMD]"]
  LED63 = smd LED [color="Red (633nm)" package="1206 [SMD]"]
  LED64 = smd LED [color="Red (633nm)" package="1206 [SMD]"]
  LED65 = smd LED [color="Red (633nm)" package="1206 [SMD]"]
  LED66 = smd LED [color="Red (633nm)" package="1206 [SMD]"]
  LED67 = smd LED [color="Red (633nm)" package="1206 [SMD]"]
  LED68 = smd LED [color="Red (633nm)" package="1206 [SMD]"]
  LED69 = smd LED [color="Red (633nm)" package="1206 [SMD]"]
  LED70 = smd LED [color="Red (633nm)" package="1206 [SMD]"]
  LED71 = smd LED [color="Red (633nm)" package="1206 [SMD]"]

nets:
  N1: U19.Q1, J470.pin2
  N2: U19.Q2, J470.pin3
  N3: U19.Q3, J470.pin4
  N4: U19.Q4, J469.pin1
  N5: U19.Q5, J469.pin2
  N6: U19.Q6, J469.pin3
  N7: U19.Q7, J469.pin4
  GND: U19.GND, U19.OE, U20.GND, U20.OE, U21.GND, U21.OE, C15.0, Part18.GND, J465.pin2, J473.pin3, J474.pin1
  VCC: U19.MR, U19.VCC, U20.MR, U20.VCC, U21.MR, U21.VCC, Part18.5V, J474.pin2
  N8: U19.SH_CP, U20.SH_CP, U21.SH_CP, Part18.A3
  N9: U19.ST_CP, U20.ST_CP, U21.ST_CP, C15.1, Part18.A2
  N10: U19.DS, U20.Q7'
  N11: U19.Q0, J470.pin1
  N12: U20.Q1, J471.pin2
  N13: U20.Q2, J471.pin3
  N14: U20.Q3, J471.pin4
  N15: U20.Q4, J467.pin1
  N16: U20.Q5, J467.pin2
  N17: U20.Q6, J467.pin3
  N18: U20.Q7, J467.pin4
  N19: U20.DS, U21.Q7'
  N20: U20.Q0, J471.pin1
  N21: U21.Q1, J468.pin2
  N22: U21.Q2, J468.pin3
  N23: U21.Q3, J468.pin4
  N24: U21.Q4, J472.pin1
  N25: U21.Q5, J472.pin2
  N26: U21.Q6, J472.pin3
  N27: U21.Q7, J472.pin4
  N28: U21.DS, Part18.A1
  N29: U21.Q0, J468.pin1
  N30: Part18.D1/TX, J466.pin1
  N31: Part18.D0/RX, J466.pin2
  N32: Part18.D2, J474.pin3
  N33: Part18.D3, J474.pin4
  N34: Part18.D10, J473.pin4
  N35: Part18.D11/MOSI, J473.pin2
  N36: Part18.D12/MISO, J473.pin1
  N37: Part18.3V3, J465.pin1
  N38: R91.Pin_0, J485.pin1
  N39: R91.Pin_1, J478.pin1
  N40: R92.Pin_0, J483.pin6
  N41: R92.Pin_1, J481.pin2
  N42: R93.Pin_0, J483.pin7
  N43: R93.Pin_1, J481.pin3
  N44: R94.Pin_0, J483.pin8
  N45: R94.Pin_1, J481.pin4
  N46: R95.Pin_0, J483.pin5
  N47: R95.Pin_1, J481.pin1
  N48: R96.Pin_0, J483.pin3
  N49: R96.Pin_1, J482.pin3
  N50: R97.Pin_0, J483.pin2
  N51: R97.Pin_1, J482.pin2
  N52: R98.Pin_0, J483.pin1
  N53: R98.Pin_1, J482.pin1
  N54: R99.Pin_0, J483.pin4
  N55: R99.Pin_1, J482.pin4
  N56: R100.Pin_0, J485.pin4
  N57: R100.Pin_1, J478.pin4
  N58: R101.Pin_0, J485.pin5
  N59: R101.Pin_1, J477.pin1
  N60: R102.Pin_0, J485.pin3
  N61: R102.Pin_1, J478.pin3
  N62: R103.Pin_0, J485.pin2
  N63: R103.Pin_1, J478.pin2
  N64: R104.Pin_0, J479.pin1
  N65: R104.Pin_1, J475.pin1
  N66: R105.Pin_0, J485.pin8
  N67: R105.Pin_1, J477.pin4
  N68: R106.Pin_0, J485.pin7
  N69: R106.Pin_1, J477.pin3
  N70: R107.Pin_0, J485.pin6
  N71: R107.Pin_1, J477.pin2
  N72: R108.Pin_0, J479.pin2
  N73: R108.Pin_1, J475.pin2
  N74: R109.Pin_0, J479.pin3
  N75: R109.Pin_1, J475.pin3
  N76: R110.Pin_0, J479.pin4
  N77: R110.Pin_1, J475.pin4
  N78: R111.Pin_0, J480.pin1
  N79: R111.Pin_1, J475.pin5
  N80: R112.Pin_0, J480.pin2
  N81: R112.Pin_1, J475.pin6
  N82: R113.Pin_0, J480.pin3
  N83: R113.Pin_1, J475.pin7
  N84: R114.Pin_0, J480.pin4
  N85: R114.Pin_1, J475.pin8
  N86: RE5.EncoderPinA, J488.pin4
  N87: RE5.EncoderPinC, J488.pin2, J489.pin1
  N88: RE5.EncoderPinB, J488.pin1
  N89: J476.pin1, LED60.anode
  N90: J476.pin2, LED67.anode
  N91: J476.pin3, LED57.anode
  N92: J476.pin4, LED50.anode
  N93: J476.pin5, LED71.anode
  N94: J476.pin6, LED58.anode
  N95: J476.pin7, LED65.anode
  N96: J476.pin8, LED49.anode
  N97: J484.pin1, LED54.anode
  N98: J484.pin2, LED61.anode
  N99: J484.pin3, LED69.anode
  N100: J484.pin4, LED53.anode
  N101: J484.pin5, LED62.anode
  N102: J484.pin6, LED66.anode
  N103: J484.pin7, LED55.anode
  N104: J484.pin8, LED63.anode
  N105: J486.pin1, LED70.anode
  N106: J486.pin2, LED56.anode
  N107: J486.pin3, LED64.anode
  N108: J486.pin4, LED48.anode
  N109: J486.pin5, LED51.anode
  N110: J486.pin6, LED59.anode
  N111: J486.pin7, LED68.anode
  N112: J486.pin8, LED52.anode
  N113: J487.pin2, LED48.cathode, LED49.cathode, LED50.cathode, LED51.cathode, LED52.cathode, LED53.cathode, LED54.cathode, LED55.cathode, LED56.cathode, LED57.cathode, LED58.cathode, LED59.cathode, LED60.cathode, LED61.cathode, LED62.cathode, LED63.cathode, LED64.cathode, LED65.cathode, LED66.cathode, LED67.cathode, LED68.cathode, LED69.cathode, LED70.cathode, LED71.cathode
  N114: J488.pin3, J490.pin1

notes:
  +
  v2.0
  Dreamer Nano v4.0
  3
  3.3V
  GND
  74HC595
  --I2C--
  2
  D13
  Rx
  0.1uF
  Tx
  220
  17
  18
  19
  20
  21
  22
  23
  <D11
  8
  9
  10
  11
  12
  <D10
  SIG. B
  13
  14
  15
  <D12
  SIG. A
  BTN
  16
  1
  6
  5
  7
  4
  0
  this board is attached upside down to the other boards
