# Fritzing sketch sequitur (saved by Fritzing 0.8.7b)
circuit board: 5.00019cm x 5cm
circuit board: 5.00019cm x 5cm
circuit board: 5.00019cm x 5cm
circuit board: 5.00019cm x 5cm
breadboards: 1

parts:
  J193 = double row female pin header, 4 pins [form="♀ (female)"]
  J194 = female pin header, 8 pins [form="♀ (female)"]
  J195 = female pin header, 8 pins [form="♀ (female)"]
  J196 = female pin header, 8 pins [form="♀ (female)"]
  J197 = female pin header, 8 pins [form="♀ (female)"]
  J198 = female pin header, 2 pins [form="♀ (female)"]
  J199 = female pin header, 2 pins [form="♀ (female)"]
  J200 = female pin header, 2 pins [form="♀ (female)"]
  J201 = female pin header, 2 pins [form="♀ (female)"]
  J202 = female pin header, 2 pins [form="♀ (female)"]
  J203 = female pin header, 2 pins [form="♀ (female)"]
  J204 = female pin header, 2 pins [form="♀ (female)"]
  J205 = female pin header, 2 pins [form="♀ (female)"]
  J206 = female pin header, 2 pins [form="♀ (female)"]
  J207 = female pin header, 2 pins [form="♀ (female)"]
  J208 = female pin header, 2 pins [form="♀ (female)"]
  J209 = female pin header, 2 pins [form="♀ (female)"]
  J210 = female pin header, 2 pins [form="♀ (female)"]
  J211 = female pin header, 2 pins [form="♀ (female)"]
  J212 = female pin header, 2 pins [form="♀ (female)"]
  J213 = female pin header, 2 pins [form="♀ (female)"]
  J214 = female pin header, 2 pins [form="♀ (female)"]
  J215 = female pin header, 2 pins [form="♀ (female)"]
  J216 = female pin header, 2 pins [form="♀ (female)"]
  J217 = female pin header, 2 pins [form="♀ (female)"]
  J218 = female pin header, 2 pins [form="♀ (female)"]
  J219 = female pin header, 2 pins [form="♀ (female)"]
  J220 = female pin header, 2 pins [form="♀ (female)"]
  J221 = female pin header, 2 pins [form="♀ (female)"]
  J222 = female pin header, 2 pins [form="♀ (female)"]
  J223 = female pin header, 2 pins [form="♀ (female)"]
  J224 = female pin header, 2 pins [form="♀ (female)"]
  J225 = female pin header, 2 pins [form="♀ (female)"]
  J226 = female pin header, 2 pins [form="♀ (female)"]
  J227 = female pin header, 2 pins [form="♀ (female)"]
  J228 = female pin header, 2 pins [form="♀ (female)"]
  J229 = female pin header, 2 pins [form="♀ (female)"]
  J230 = female pin header, 2 pins [form="♀ (female)"]
  J231 = female pin header, 1 pin [form="♀ (female)"]
  J232 = female pin header, 1 pin [form="♀ (female)"]
  J233 = female pin header, 1 pin [form="♀ (female)"]  # not connected
  J234 = female pin header, 1 pin [form="♀ (female)"]
  J235 = female pin header, 1 pin [form="♀ (female)"]  # not connected
  J236 = female pin header, 1 pin [form="♀ (female)"]
  J237 = female pin header, 1 pin [form="♀ (female)"]
  J238 = female pin header, 1 pin [form="♀ (female)"]  # not connected
  J239 = female pin header, 1 pin [form="♀ (female)"]
  J240 = female pin header, 1 pin [form="♀ (female)"]
  J241 = female pin header, 1 pin [form="♀ (female)"]
  J242 = female pin header, 1 pin [form="♀ (female)"]  # not connected
  J243 = female pin header, 1 pin [form="♀ (female)"]
  J244 = female pin header, 1 pin [form="♀ (female)"]  # not connected
  J245 = female pin header, 1 pin [form="♀ (female)"]
  J246 = female pin header, 1 pin [form="♀ (female)"]
  J247 = female pin header, 1 pin [form="♀ (female)"]
  J248 = female pin header, 1 pin [form="♀ (female)"]  # not connected
  J249 = female pin header, 1 pin [form="♀ (female)"]  # not connected
  J250 = female pin header, 1 pin [form="♀ (female)"]
  J251 = female pin header, 1 pin [form="♀ (female)"]
  J252 = female pin header, 1 pin [form="♀ (female)"]
  J253 = female pin header, 1 pin [form="♀ (female)"]  # not connected
  J254 = female pin header, 1 pin [form="♀ (female)"]
  J255 = female pin header, 1 pin [form="♀ (female)"]  # not connected
  J256 = female pin header, 1 pin [form="♀ (female)"]  # not connected
  J257 = female pin header, 1 pin [form="♀ (female)"]
  J258 = female pin header, 1 pin [form="♀ (female)"]
  J259 = female pin header, 1 pin [form="♀ (female)"]
  J260 = female pin header, 1 pin [form="♀ (female)"]
  J261 = female pin header, 1 pin [form="♀ (female)"]
  J262 = female pin header, 1 pin [form="♀ (female)"]  # not connected
  J263 = female pin header, 1 pin [form="♀ (female)"]
  J264 = female pin header, 1 pin [form="♀ (female)"]
  J265 = female pin header, 1 pin [form="♀ (female)"]  # not connected
  J266 = female pin header, 1 pin [form="♀ (female)"]
  J267 = female pin header, 1 pin [form="♀ (female)"]
  J268 = female pin header, 1 pin [form="♀ (female)"]  # not connected
  J269 = female pin header, 1 pin [form="♀ (female)"]
  J270 = female pin header, 1 pin [form="♀ (female)"]
  J271 = female pin header, 1 pin [form="♀ (female)"]  # not connected
  J272 = female pin header, 1 pin [form="♀ (female)"]
  J273 = female pin header, 1 pin [form="♀ (female)"]  # not connected
  J274 = female pin header, 1 pin [form="♀ (female)"]  # not connected
  J275 = female pin header, 1 pin [form="♀ (female)"]
  J276 = female pin header, 1 pin [form="♀ (female)"]
  J277 = female pin header, 1 pin [form="♀ (female)"]
  J278 = female pin header, 1 pin [form="♀ (female)"]
  R35 = Resistor [tolerance=±5% resistance=10k package=THT]
  R36 = Resistor [tolerance=±5% resistance=10k package=THT]
  R37 = Resistor [tolerance=±5% resistance=10k package=THT]
  R38 = Resistor [tolerance=±5% resistance=10k package=THT]
  R39 = Resistor [tolerance=±5% resistance=10k package=THT]
  R40 = Resistor [tolerance=±5% resistance=10k package=THT]
  R41 = Resistor [tolerance=±5% resistance=10k package=THT]
  R42 = Resistor [tolerance=±5% resistance=10k package=THT]
  R43 = Resistor [tolerance=±5% resistance=10k package=THT]
  R44 = Resistor [tolerance=±5% resistance=10k package=THT]
  R45 = Resistor [tolerance=±5% resistance=10k package=THT]
  R46 = Resistor [tolerance=±5% resistance=10k package=THT]
  R47 = Resistor [tolerance=±5% resistance=10k package=THT]
  R48 = Resistor [tolerance=±5% resistance=10k package=THT]
  R49 = Resistor [tolerance=±5% resistance=10k package=THT]
  R50 = Resistor [tolerance=±5% resistance=10k package=THT]
  Part9 = Arduino Nano (Rev3.0)
  J454 = double row female pin header, 4 pins [form="♀ (female)"]
  J455 = female pin header, 8 pins [form="♀ (female)"]
  J456 = female pin header, 8 pins [form="♀ (female)"]
  J457 = female pin header, 2 pins [form="♀ (female)"]
  Part11 = Arduino Nano (Rev3.0)
  J458 = female pin header, 2 pins [form="♀ (female)"]
  J459 = female pin header, 2 pins [form="♀ (female)"]

nets:
  N1: J193.pin1, J212.pin2, Part9.GND
  N2: J193.pin2, J212.pin1, Part9.5V
  N3: J193.pin3, Part9.A4
  N4: J193.pin4, Part9.A5
  N5: J194.pin1, J201.pin2
  N6: J194.pin2, J201.pin1
  N7: J194.pin3, J214.pin2
  N8: J194.pin4, J214.pin1
  N9: J194.pin5, J206.pin2
  N10: J194.pin6, J206.pin1
  N11: J194.pin7, J210.pin2
  N12: J194.pin8, J210.pin1
  N13: J195.pin1, Part9.D9
  N14: J195.pin2, Part9.D8
  N15: J195.pin3, Part9.D7
  N16: J195.pin4, Part9.D6
  N17: J195.pin5, Part9.D5
  N18: J195.pin6, Part9.D4
  N19: J195.pin7, Part9.D3
  N20: J195.pin8, Part9.D2
  N21: J196.pin1, J200.pin2
  N22: J196.pin2, J200.pin1
  N23: J196.pin3, J203.pin2
  N24: J196.pin4, J203.pin1
  N25: J196.pin5, J202.pin2
  N26: J196.pin6, J202.pin1
  N27: J196.pin7, J199.pin2
  N28: J196.pin8, J199.pin1
  N29: J197.pin1, Part9.D13/SCK
  N30: J197.pin2, Part9.A0
  N31: J197.pin3, Part9.A1
  N32: J197.pin4, Part9.A2
  N33: J197.pin5, Part9.A3
  N34: J197.pin6, Part9.D12/MISO
  N35: J197.pin7, Part9.D11/MOSI
  N36: J197.pin8, Part9.D10
  N37: J198.pin1, J204.pin1, J205.pin1, J207.pin1, J208.pin1, J209.pin1, J211.pin1, J213.pin1
  N38: J198.pin2, J204.pin2, J205.pin2, J207.pin2, J208.pin2, J209.pin2, J211.pin2, J213.pin2
  N39: J215.pin1, J251.pin1, R42.Pin_0
  N40: J215.pin2, R43.Pin_1
  N41: J216.pin1, J250.pin1
  N42: J216.pin2, J254.pin1
  N43: J217.pin1, J232.pin1, R37.Pin_1
  N44: J217.pin2, R38.Pin_0
  N45: J218.pin1, J234.pin1, R40.Pin_1
  N46: J218.pin2, J236.pin1
  N47: J219.pin1, J237.pin1, R39.Pin_1
  N48: J219.pin2, J240.pin1
  N49: J220.pin1, J241.pin1, R40.Pin_0
  N50: J220.pin2, R44.Pin_1
  N51: J221.pin1, J246.pin1, R39.Pin_0
  N52: J221.pin2, R41.Pin_1
  N53: J222.pin1, J245.pin1, R42.Pin_1
  N54: J222.pin2, J247.pin1
  N55: J223.pin1, J259.pin1, R46.Pin_0
  N56: J223.pin2, R45.Pin_1
  N57: J224.pin1, J260.pin1
  N58: J224.pin2, J257.pin1
  N59: J225.pin1, J266.pin1, R48.Pin_0
  N60: J225.pin2, R47.Pin_1
  N61: J226.pin1, J263.pin1, R37.Pin_0, R46.Pin_1
  N62: J226.pin2, J264.pin1
  N63: J227.pin1, J270.pin1, R48.Pin_1
  N64: J227.pin2, J272.pin1
  N65: J228.pin1, J269.pin1, R49.Pin_0
  N66: J228.pin2, R50.Pin_1
  N67: J229.pin1, J275.pin1, R35.Pin_1
  N68: J229.pin2, R36.Pin_0
  N69: J230.pin1, J278.pin1, R35.Pin_0, R49.Pin_1
  N70: J230.pin2, J276.pin1
  N71: J231.pin1, R38.Pin_1
  N72: J239.pin1, R44.Pin_0
  N73: J243.pin1, R41.Pin_0
  N74: J252.pin1, R43.Pin_0
  N75: J258.pin1, R45.Pin_0
  N76: J261.pin1, R47.Pin_0
  N77: J267.pin1, R50.Pin_0
  N78: J277.pin1, R36.Pin_1
  N79: J454.pin1, J457.pin2, Part11.GND, J458.pin2
  N80: J454.pin2, J457.pin1, Part11.5V
  N81: J454.pin3, Part11.D2
  N82: J454.pin4, Part11.D3
  N83: J455.pin1, Part11.D9
  N84: J455.pin2, Part11.D8
  N85: J455.pin3, Part11.D7
  N86: J455.pin4, Part11.D6
  N87: J455.pin5, Part11.D5
  N88: J455.pin6, Part11.D4
  N89: J455.pin7, Part11.A5
  N90: J455.pin8, Part11.A4
  N91: J456.pin1, Part11.D13/SCK
  N92: J456.pin2, Part11.A0
  N93: J456.pin3, Part11.A1
  N94: J456.pin4, Part11.A2
  N95: J456.pin5, Part11.A3
  N96: J456.pin6, Part11.D12/MISO
  N97: J456.pin7, Part11.D11/MOSI
  N98: J456.pin8, Part11.D10
  N99: Part11.D1/TX, J459.pin1
  N100: Part11.D0/RX, J459.pin2
  N101: Part11.3V3, J458.pin1

notes:
  LED2
  LED1
  BTN1
  > D8
  > D9
  BTN4
  LED3
  > D5
  LED4
  > D4
  BTN3
  > D7
  > D3
  > D2
  BTN2
  > D6`
  D13
  10k
  220
  BTN 5
  LED 5
  BTN 6
  LED 6
  BTN 7
  LED 7
  D11 <
  D10 <
  BTN8
  LED8
  BTN 8
  LED 8
  BTN 4
  A5
  A4
  LED6
  D13 <
  LED5
  A1 <
  A0 <
  LED 4
  BTN7
  D12 <
  A3 <
  LED7
  A2 <
  BTN5
  LED 3
  BTN 3
  BTN 2
  LED 2
  +
  GND
  --I2C--
  BTN6
  BTN 1
  LED 1
  this board is attached upside down to the other board. this is the old version. for reference only
  > A5
  > A4
  Dreamer Nano v4.0
  > D6
  v2.0
  3
  2
  Rx
  Tx
  3.3V
  alternate board v2.0 with different connections for I2C for nano/dreamer
  v1.0
